# Fritzing sketch Omni_Robot_sch (saved by Fritzing 0.9.9b)
breadboards: 1

parts:
  Parts1 = SparkFun RedBoard [part_number=DEV-12757]  # not connected
  Part1 = Adafruit Motor/Stepper/Servo Shield [part_number="Adafruit #1438"]
  Part2 = Bluetooth HC-05 Macho
  3-Axis_Accelerometer1 = 3-Axis Accelerometer Breakout - MMA8452Q
  Part3 = Logic Level Converter
  Part4 = Módulo Relé
  LED1 = smd LED [color="Red (633nm)" package="0603 [SMD]"]
  LED2 = smd LED [color="Blue (505nm)" package="0603 [SMD]"]
  R1 = Resistor [tolerance=±5% resistance=220 package="2010 [SMD]"]
  R2 = Resistor [tolerance=±5% resistance=220 package="2010 [SMD]"]
  M1 = gear-motor
  M2 = gear-motor
  M3 = gear-motor
  M4 = gear-motor
  VCC1 = Battery
  INA1 = INA219 DC Current Sensor Breakout
  S1 = Toggle Switch [package=THT]

nets:
  N1: Part1.M2A, M2.pin_1
  N2: Part1.M2B, M2.pin_2
  N3: Part1.M1B, M1.pin_1
  N4: Part1.M1A, M1.pin_2
  N5: Part1.M3A, M3.pin_2
  N6: Part1.M3B, M3.pin_1
  N7: Part1.M4B, M4.pin_2
  N8: Part1.M4A, M4.pin_1
  VCC: Part1.+5V, Part2.VCC, Part3.HV, Part4.5V, Part4.C, INA1.VCC
  GND: Part1.GND, Part2.GND, 3-Axis_Accelerometer1.GND, Part3.GND, Part4.GND, LED1.cathode, LED2.cathode, VCC1.-, INA1.GND
  N9: Part1.VMOTOR, INA1.Vin-2
  N10: Part1.D10, Part4.In
  +3V3: Part1.+3V3, 3-Axis_Accelerometer1.3.3V, Part3.LV
  N11: Part1.AD4/SDA, Part3.RX_HV, INA1.SDA
  N12: Part1.AD5/SCL, Part3.TX_HV, INA1.SCL
  N13: Part1.D2, Part3.TX2_HV
  N14: Part1.D3, Part3.RX2_HV
  N15: Part2.TXD, Part3.RX2_LV
  N16: Part2.RXD, Part3.TX2_LV
  N17: 3-Axis_Accelerometer1.SDA, Part3.TX_LV
  N18: 3-Axis_Accelerometer1.SCL, Part3.RX_LV
  N19: Part4.NA, R1.Pin_0, R2.Pin_0
  N20: INA1.Vin+2, S1.COM

custom parts:
  SparkFun RedBoard: At SparkFun we use many Arduinos and we’re always looking for the simplest, most stable one. Each board is a bit different and no one board has everything we want, so we decided to make our own version that combines all our favorite features. The RedBoard combines the simplicity of the UNO’s Optiboot bootloader (which is used in the Pro series), the stability of the FTDI (which we all missed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
  Adafruit Motor/Stepper/Servo Shield: The original Adafruit Motorshield kit is one of our most beloved kits, which is why we decided to make something even better. We have upgraded the shield kit to make the bestest, easiest way to drive DC and Stepper motors. This shield will make quick work of your next robotics project! We kept the ability to drive up to 4 DC motors or 2 stepper motors, but added many improvements: Instead of a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
  Logic Level Converter: Description: If you've ever tried to connect a 3.3V device to a 5V system, you know what a challenge it can be. The SparkFun logic level converter is a small device that safely steps down 5V signals to 3.3V and steps up 3.3V to 5V. This level converter also works with 2.8V and 1.8V devices. Each level converter has the capability of converting 4 pins on the high side to 4 pins on the low side.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
  Módulo Relé: Este modulo pode ser usado em diversos projetos afim de acionar cargas de até 250VAC @ 7A ou 125VAC @ 10A. Pode ser usado para controlar luzes, equipamentos ligados a rede elétrica, motores, etc. Você pode fazer uma ponte-H baseada em relés com alguns destes módulos.
  Battery: Your standard 2x 18650 battery pack (7,4 Volts)
  INA219 DC Current Sensor Breakout: INA DC Current Sensor Breakout
